# Fritzing sketch Laser Viscometer (saved by Fritzing 0.9.3b)
breadboards: 1

parts:
  Part1 = Arduino Nano (Rev3.0)
  LD1 = LD
  LD2 = LD
  P1 = S1133 Si Photodiode [package="8mm Ceramic [THT]"]
  P2 = S1133 Si Photodiode [package="8mm Ceramic [THT]"]
  R1 = Resistor [tolerance=±5% resistance=100k package=THT]
  R2 = Resistor [tolerance=±5% resistance=100k package=THT]
  S1 = Momentary Switch [package=ksa_sealed_tac_switch]
  R3 = Resistor [tolerance=±5% resistance=100k package=THT]

nets:
  N1: Part1.GND, LD1.cathode, LD2.cathode, R1.Pin_1, R2.Pin_1, R3.Pin_1
  N2: Part1.D2, P1.cathode, R2.Pin_0
  N3: Part1.D3, P2.cathode, R1.Pin_0
  N4: Part1.D4, S1.3, R3.Pin_0
  N5: Part1.5V, P1.anode, P2.anode, S1.2
  N6: Part1.D13/SCK, LD1.anode, LD2.anode

custom parts:
  LD: A Generic Red Dot Laser Diode Module (~5mW)
